# Fritzing sketch ESP8266-programmer (saved by Fritzing 0.9.4)
circuit board: 8.46667cm x 5.64444cm
breadboards: 1

parts:
  Gizwits_WiFi_Witty_ESP-12F1 = Gizwits WiFi Witty ESP-12F
  S1 = Pushbutton [package="[THT]"]
  USB_Programmer = FTDI Basic Programmer
  R2 = Resistor [tolerance=±5% resistance=10k package=THT]
  R3 = Resistor [tolerance=±5% resistance=10k package=THT]
  J1 = shrouded pin header, 8 pins [form="♂ (shrouded male)"]

nets:
  N1: Gizwits_WiFi_Witty_ESP-12F1.REST, S1.Pin_1, S1.Pin_2, R3.Pin_1
  3.3V: Gizwits_WiFi_Witty_ESP-12F1.CH_PD, Gizwits_WiFi_Witty_ESP-12F1.VCC, R3.Pin_0, J1.pin4
  GND: Gizwits_WiFi_Witty_ESP-12F1.GND, S1.Pin_3, S1.Pin_4, USB_Programmer.GND, R2.Pin_1, J1.pin8
  N2: Gizwits_WiFi_Witty_ESP-12F1.GPIO0, R2.Pin_0
  N3: Gizwits_WiFi_Witty_ESP-12F1.RXD, USB_Programmer.RXI, J1.pin5
  N4: Gizwits_WiFi_Witty_ESP-12F1.TXD, USB_Programmer.TXO, J1.pin1
